// Logisim project dom2.circ as structural Verilog: 4 circuits, main circuit unos
module unos (
  input  X16,
  input  X8,
  input  X4,
  input  X2,
  input  X1,
  output Y
);


  // Notes on the sheet:
  //   19.11.
  //   1+9+1+1=12
  //   12=01100
  //   6.korak: Brišem nepotrebna NILI kola.
  //   1. korak: Sabiram cifre datuma rođenja, i sumu prebacujem u binarni brojni sistem.
  //   3. korak: Kreiram šemu sa dvoulaznim kolima pomoću tablice.
  //   5.korak: Crtam šemu ispočetka sa NILI kolima i proveravam rezultat u tablici.
  //   4. korak: Svako NI kolo prebacujem u odgovarajuće NILI kolo, a svako I kolo u odgovarajuću kombinaciju NILI kola.
  //   2. korak: Definišem 5 ulaza i 1 izlaz, u tablici navodim da je izlaz uvek nula osim u slučaju kada su ulazi {X4,X8}=1, a {X16,X2,X1}=0
endmodule

module dvoulazno_I (
  input  X16,
  input  X8,
  input  X4,
  input  X2,
  input  X1,
  output Y
);

  wire and_1_out, and_2_out, and_4_out, not_1_out, not_2_out, not_3_out;

  not not_1 (not_1_out, X16);
  and and_1 (and_1_out, not_1_out, X8);
  not not_2 (not_2_out, X2);
  not not_3 (not_3_out, X1);
  and and_2 (and_2_out, and_1_out, X4);
  and and_3 (Y, and_2_out, and_4_out);
  and and_4 (and_4_out, not_2_out, not_3_out);

  // Notes on the sheet:
  //   6.korak: Brišem nepotrebna NILI kola.
  //   3. korak: Kreiram šemu sa dvoulaznim kolima pomoću tablice.
  //   5 korak: Crtam šemu ispočetka sa NILI kolima i proveravam rezultat u tablici.
  //   1. korak: Sabiram cifre datuma rođenja, i sumu prebacujem u binarni brojni sistem.
  //   2. korak: Definišem 5 ulaza i 1 izlaz, u tablici navodim da je izlaz uvek nula osim u slučaju kada su ulazi {X4,X8}=1, a {X16,X2,X1}=0
  //   4. korak: Svako NI kolo prebacujem u odgovarajuće NILI kolo, a svako I kolo u odgovarajuću kombinaciju NILI kola.
endmodule

module samo_NILI (
  input  X16,
  input  X8,
  input  X4,
  input  X2,
  input  X1,
  output Y
);

  wire nor_1_out, nor_2_out, nor_3_out, nor_4_out, nor_5_out, nor_6_out, nor_7_out, nor_8_out, nor_9_out,
       nor_10_out, nor_11_out, nor_12_out, nor_13_out, nor_14_out;

  nor nor_1 (nor_1_out, X16, X16);
  nor nor_2 (nor_2_out, X2, X2);
  nor nor_3 (nor_3_out, X1, X1);
  nor nor_4 (nor_4_out, nor_1_out, nor_1_out);
  nor nor_5 (nor_5_out, X8, X8);
  nor nor_6 (nor_6_out, nor_2_out, nor_2_out);
  nor nor_7 (nor_7_out, nor_3_out, nor_3_out);
  nor nor_8 (nor_8_out, nor_4_out, nor_5_out);
  nor nor_9 (nor_9_out, nor_6_out, nor_7_out);
  nor nor_10 (nor_10_out, nor_8_out, nor_8_out);
  nor nor_11 (nor_11_out, X4, X4);
  nor nor_12 (nor_12_out, nor_10_out, nor_11_out);
  nor nor_13 (nor_13_out, nor_12_out, nor_12_out);
  nor nor_14 (nor_14_out, nor_9_out, nor_9_out);
  nor nor_15 (Y, nor_13_out, nor_14_out);

  // Notes on the sheet:
  //   6.korak: Brišem nepotrebna NILI kola.
  //   3. korak: Kreiram šemu sa dvoulaznim kolima pomoću tablice.
  //   1. korak: Sabiram cifre datuma rođenja, i sumu prebacujem u binarni brojni sistem.
  //   5. korak: Crtam šemu ispočetka sa NILI kolima i proveravam rezultat u tablici.
  //   2. korak: Definišem 5 ulaza i 1 izlaz, u tablici navodim da je izlaz uvek nula osim u slučaju kada su ulazi {X4,X8}=1, a {X16,X2,X1}=0
  //   4. korak: Svako NI kolo prebacujem u odgovarajuće NILI kolo, a svako I kolo u odgovarajuću kombinaciju NILI kola.
endmodule

module \konačno_kolo  (
  input  X16,
  input  X8,
  input  X4,
  input  X2,
  input  X1,
  output Y
);

  wire nor_1_out, nor_2_out, nor_3_out, nor_4_out, nor_5_out, nor_6_out, nor_7_out, nor_8_out;

  nor nor_1 (nor_1_out, X8, X8);
  nor nor_2 (nor_2_out, X16, nor_1_out);
  nor nor_3 (nor_3_out, X2, X1);
  nor nor_4 (nor_4_out, nor_2_out, nor_2_out);
  nor nor_5 (nor_5_out, X4, X4);
  nor nor_6 (nor_6_out, nor_4_out, nor_5_out);
  nor nor_7 (nor_7_out, nor_6_out, nor_6_out);
  nor nor_8 (nor_8_out, nor_3_out, nor_3_out);
  nor nor_9 (Y, nor_7_out, nor_8_out);

  // Notes on the sheet:
  //   6.korak: Brišem nepotrebna NILI kola.
  //   3. korak: Kreiram šemu sa dvoulaznim kolima pomoću tablice.
  //   1. korak: Sabiram cifre datuma rođenja, i sumu prebacujem u binarni brojni sistem.
  //   5.korak: Crtam šemu ispočetka sa NILI kolima i proveravam rezultat u tablici.
  //   2. korak: Definišem 5 ulaza i 1 izlaz, u tablici navodim da je izlaz uvek nula osim u slučaju kada su ulazi {X4,X8}=1, a {X16,X2,X1}=0
  //   4. korak: Svako NI kolo prebacujem u odgovarajuće NILI kolo, a svako I kolo u odgovarajuću kombinaciju NILI kola.
endmodule
